# Fritzing sketch schematic (saved by Fritzing 0.9.3b)

parts:
  Part2 = Arduino Nano (Rev3.0)
  HLK-PM1 = HLK-PM01
  U1 = V18ZA2P [package=v18za2p]
  Part3 = ACS712 Low Current Sensor Board v12
  J1 = Screw terminal - 2 pins [package=THT]
  J2 = Screw terminal - 2 pins [package=THT]
  YL-1 = YL-105 [part_number=YL-105]
  Part4 = NRF24L01+ Breakout Board  # not connected
  S1 = Round Pushbutton
  R1 = Resistor [tolerance=±5% resistance=220 package="0603 [SMD]"]
  LED1 = LED - 3mm [color="Red (633nm)" package="3 mm [THT]"]
  Part5 = Arduino Nano (Rev3.0)
  YL-2 = YL-105 [part_number=YL-105]
  Part6 = NRF24L01+ Breakout Board  # not connected
  J3 = Screw terminal - 2 pins [package=THT]
  KY-1 = Keyes Relay [package=THT]
  J4 = Screw terminal - 2 pins [package=THT]
  F1 = FUSE [package=fuse_5mm]
  LED2 = LED - 3mm [color="Red (633nm)" package="3 mm [THT]"]
  R2 = Resistor [tolerance=±5% resistance=220 package="0603 [SMD]"]
  C1 = Electrolytic Capacitor [capacitance=100µF package="200 mil [THT, electrolytic]"]
  J5 = Screw terminal - 2 pins [package=THT]
  J6 = Screw terminal - 2 pins [package=THT]
  J7 = Screw terminal - 2 pins [package=THT]

nets:
  N1: Part2.D3, S1.leg0
  N2: Part2.D4, R1.Pin_1
  N3: Part2.D9, YL-1.CE
  N4: Part2.D10, YL-1.CSN
  N5: Part2.D11/MOSI, YL-1.MOSI
  N6: Part2.D12/MISO, YL-1.MISO
  VIN: Part2.VIN, Part3.5V, YL-1.VCC, J6.pin2
  GND: Part2.GND, Part3.GND, YL-1.GND, S1.leg1, LED1.cathode, J6.pin1
  N7: Part2.A0, Part3.VO
  N8: Part2.D13/SCK, YL-1.SCK
  N9: HLK-PM1.AC#0, U1.P$1, F1.2
  N10: HLK-PM1.AC#1, U1.P$2, J5.pin1
  N11: HLK-PM1.-Vo, C1.-
  N12: HLK-PM1.+Vo, C1.+
  N13: Part3.IP+, J1.pin2
  N14: Part3.IP-, J2.pin1
  N15: J1.pin1, J2.pin2
  N16: R1.Pin_0, LED1.anode
  N17: Part5.D2, YL-2.IRQ
  N18: Part5.D3, R2.Pin_0
  N19: Part5.D4, KY-1.signal
  N20: Part5.D8, Part5.D9, YL-2.CE
  N21: Part5.D10, YL-2.CSN
  N22: Part5.D11/MOSI, YL-2.MOSI
  N23: Part5.D12/MISO, YL-2.MISO
  VIN_2: Part5.VIN, YL-2.VCC, KY-1.power, J7.pin1
  GND_2: Part5.GND, YL-2.GND, KY-1.ground, LED2.cathode, J7.pin2
  N24: Part5.D13/SCK, YL-2.SCK
  N25: J3.pin1, KY-1.C
  N26: J3.pin2, J4.pin1
  N27: KY-1.NO, J4.pin2
  N28: F1.1, J5.pin2
  N29: LED2.anode, R2.Pin_1

notes:
  AC 220v
  Table Saw
  Transmitter
  Vacuum
  Receiver
  500mA Fuse
  Varistor
  ACS712 30A
  Current Sensor
  Toggle Switch
  Radio Communication
  5V Relay
  NRF24L01
  GND
  5V
  Power Supply
  DC 5V
  Status

custom parts:
  Keyes Relay: The Keyes 5V relay module is suitable for SCM development, home appliance control. It uses a 5V~12V TIL control signal which can control DC / AC signal.
